// Logisim project qtictactoe.circ as structural Verilog: 16 circuits, main circuit main
module main (
);

  wire engine_1_p5, engine_1_p6, engine_1_p7, engine_1_p8, engine_1_p9, engine_1_p10, engine_1_p11,
       P2_is_out, RESET_out, t_ff_1_q, t_ff_1_qn, t_ff_2_q, t_ff_2_qn, Who_starts_out;
  wire [8:0] button_2_out, engine_1_p12, engine_1_p13;

  LED P2 (.in(t_ff_1_q));
  LED P1 (.in(t_ff_1_qn));
  Button Who_starts (.out(Who_starts_out));
  LED Computer (.in(t_ff_2_q));
  LED Player (.in(t_ff_2_qn));
  Button P2_is (.out(P2_is_out));
  Button button_1 (.out(button_2_out[1]));
  Button button_2 (.out(button_2_out[0]));
  Button button_3 (.out(button_2_out[3]));
  Button button_4 (.out(button_2_out[4]));
  Button button_5 (.out(button_2_out[6]));
  Button button_6 (.out(button_2_out[7]));
  LED led_1 (.in(button_2_out[0]));
  LED led_2 (.in(button_2_out[3]));
  LED led_3 (.in(button_2_out[6]));
  Button button_7 (.out(button_2_out[2]));
  Button button_8 (.out(button_2_out[5]));
  Button button_9 (.out(button_2_out[8]));
  LED led_4 (.in(button_2_out[2]));
  LED led_5 (.in(button_2_out[1]));
  LED led_6 (.in(button_2_out[4]));
  LED led_7 (.in(button_2_out[5]));
  LED led_8 (.in(button_2_out[8]));
  LED led_9 (.in(button_2_out[7]));
  T_Flip_Flop t_ff_1 (.clk(Who_starts_out), .T(1'b1), .Q(t_ff_1_q), .Qn(t_ff_1_qn));  // open: preset, reset, en
  T_Flip_Flop t_ff_2 (.clk(P2_is_out), .T(1'b1), .Q(t_ff_2_q), .Qn(t_ff_2_qn));  // open: preset, reset, en
  Button RESET (.out(RESET_out));
  LED P1_TURN (.in(engine_1_p5));
  LED P2_TURN (.in(engine_1_p6));
  LED START (.in(engine_1_p7));
  LED OVER (.in(engine_1_p8));
  // ENGINE engine_1: pin names not known; wires that end beside it: t_ff_1_q, t_ff_2_q, RESET_out, button_2_out, engine_1_p5, engine_1_p6, engine_1_p7, engine_1_p8, engine_1_p9, engine_1_p10, engine_1_p11, engine_1_p12, engine_1_p13
  LED P1_WON (.in(engine_1_p9));
  LED P2_WON (.in(engine_1_p10));
  LED DRAW (.in(engine_1_p11));
  LED led_10 (.in(engine_1_p12[0]));
  LED led_11 (.in(engine_1_p12[3]));
  LED led_12 (.in(engine_1_p12[6]));
  LED led_13 (.in(engine_1_p13[0]));
  LED led_14 (.in(engine_1_p13[3]));
  LED led_15 (.in(engine_1_p13[6]));
  LED led_16 (.in(engine_1_p13[1]));
  LED led_17 (.in(engine_1_p12[1]));
  LED led_18 (.in(engine_1_p12[4]));
  LED led_19 (.in(engine_1_p13[4]));
  LED led_20 (.in(engine_1_p12[7]));
  LED led_21 (.in(engine_1_p13[7]));
  LED led_22 (.in(engine_1_p12[2]));
  LED led_23 (.in(engine_1_p13[2]));
  LED led_24 (.in(engine_1_p13[5]));
  LED led_25 (.in(engine_1_p12[5]));
  LED led_26 (.in(engine_1_p13[8]));
  LED led_27 (.in(engine_1_p12[8]));

  // Notes on the sheet:
  //   IMPORTANT: START SIMULATION!
  //   Make sure tick frequency is >256hz
  //   (Simulate->Tick Frequency)
  //   Make sure ticks are enabled
  //   (Simulate->Ticks Enabled)
  //   Make sure simulation is enabled
  //   (Simulate->Simulation Enabled)
endmodule

module ENGINE (
  input  P2_is_starting,
  input  isComputer,
  input  RESET,
  input  [8:0] MOV_SLCT_INPUT,
  output P1_TURN,
  output P2_TURN,
  output OVER,
  output P1_WON,
  output P2_WON,
  output DRAW,
  output [8:0] BOARD_P1,
  output [8:0] BOARD_P2
);

  wire CLK, p_mov_ok_1_player_move_ok, undriven;
  wire [8:0] cpu_1_cpu, p2_switch_1_out;

  Clock clock_1 (.out(CLK));
  P2_SWITCH p2_switch_1 (.PLR_MOV(MOV_SLCT_INPUT), .CPU_MOV(cpu_1_cpu), .doAI(isComputer), .OUT(p2_switch_1_out));
  BOARD_MEM_1 board_mem_1_1 (.RESET(RESET), .CLK(CLK), .INP(MOV_SLCT_INPUT), .STATE(BOARD_P1));  // open: EN
  BOARD_MEM_1 board_mem_1_2 (.RESET(RESET), .EN(undriven), .CLK(CLK), .INP(p2_switch_1_out), .STATE(BOARD_P2));
  END_DTCT end_dtct_1 (.P1(BOARD_P1), .P2(BOARD_P2), .P1_WIN(P1_WON), .P2_WIN(P2_WON), .DRAW(DRAW), .GAME_OVER(OVER));
  P_MOV_OK p_mov_ok_1 (
    .B1_state(BOARD_P1), .B2_state(BOARD_P2), .pmov(MOV_SLCT_INPUT),
    .Player_Move_OK(p_mov_ok_1_player_move_ok));
  CPU cpu_1 (.P1(BOARD_P1), .P2(BOARD_P2), .CPU(cpu_1_cpu));

  // Other names for the same wires on the sheet: RST = RESET
endmodule

module MOV_SELECT_MEM (
  input  [8:0] INPUT,
  output [8:0] OUTPUT
);

  wire or_1_out, or_2_out, or_3_out, or_4_out, or_5_out, or_6_out, or_7_out, or_8_out, or_9_out;

  or or_1 (or_1_out, INPUT[1], INPUT[2], INPUT[3], INPUT[4], INPUT[5], INPUT[6], INPUT[7], INPUT[8], 1'b0);
  or or_2 (or_2_out, INPUT[0], INPUT[1], INPUT[2], INPUT[4], INPUT[5], INPUT[6], INPUT[7], INPUT[8], 1'b0);
  or or_3 (or_3_out, INPUT[0], INPUT[1], INPUT[2], INPUT[3], INPUT[4], INPUT[5], INPUT[7], INPUT[8], 1'b0);
  or or_4 (or_4_out, INPUT[0], INPUT[2], INPUT[3], INPUT[4], INPUT[5], INPUT[6], INPUT[7], INPUT[8], 1'b0);
  or or_5 (or_5_out, INPUT[0], INPUT[1], INPUT[2], INPUT[3], INPUT[5], INPUT[6], INPUT[7], INPUT[8], 1'b0);
  or or_6 (or_6_out, INPUT[0], INPUT[1], INPUT[2], INPUT[3], INPUT[4], INPUT[5], INPUT[6], INPUT[8], 1'b0);
  or or_7 (or_7_out, INPUT[0], INPUT[1], INPUT[3], INPUT[4], INPUT[5], INPUT[6], INPUT[7], INPUT[8], 1'b0);
  or or_8 (or_8_out, INPUT[0], INPUT[1], INPUT[2], INPUT[3], INPUT[4], INPUT[6], INPUT[7], INPUT[8], 1'b0);
  or or_9 (or_9_out, INPUT[0], INPUT[1], INPUT[2], INPUT[3], INPUT[4], INPUT[5], INPUT[6], INPUT[7], 1'b0);
  S_R_Flip_Flop #(.trigger("high")) s_r_ff_1 (
    .S(INPUT[0]), .clk(1'b1), .R(or_1_out), .Q(OUTPUT[0]));  // open: Qn, preset, reset, en
  S_R_Flip_Flop #(.trigger("high")) s_r_ff_2 (
    .S(INPUT[3]), .clk(1'b1), .R(or_2_out), .Q(OUTPUT[3]));  // open: Qn, preset, reset, en
  S_R_Flip_Flop #(.trigger("high")) s_r_ff_3 (
    .S(INPUT[6]), .clk(1'b1), .R(or_3_out), .Q(OUTPUT[6]));  // open: Qn, preset, reset, en
  S_R_Flip_Flop #(.trigger("high")) s_r_ff_4 (
    .S(INPUT[1]), .clk(1'b1), .R(or_4_out), .Q(OUTPUT[1]));  // open: Qn, preset, reset, en
  S_R_Flip_Flop #(.trigger("high")) s_r_ff_5 (
    .S(INPUT[4]), .clk(1'b1), .R(or_5_out), .Q(OUTPUT[4]));  // open: Qn, preset, reset, en
  S_R_Flip_Flop #(.trigger("high")) s_r_ff_6 (
    .S(INPUT[7]), .clk(1'b1), .R(or_6_out), .Q(OUTPUT[7]));  // open: Qn, preset, reset, en
  S_R_Flip_Flop #(.trigger("high")) s_r_ff_7 (
    .S(INPUT[2]), .clk(1'b1), .R(or_7_out), .Q(OUTPUT[2]));  // open: Qn, preset, reset, en
  S_R_Flip_Flop #(.trigger("high")) s_r_ff_8 (
    .S(INPUT[5]), .clk(1'b1), .R(or_8_out), .Q(OUTPUT[5]));  // open: Qn, preset, reset, en
  S_R_Flip_Flop #(.trigger("high")) s_r_ff_9 (
    .S(INPUT[8]), .clk(1'b1), .R(or_9_out), .Q(OUTPUT[8]));  // open: Qn, preset, reset, en

  // Other names for the same wires on the sheet: MOVSEL_0 = INPUT[0]; MOVSEL_1 = INPUT[1]; MOVSEL_2 = INPUT[2];
  //   MOVSEL_3 = INPUT[3]; MOVSEL_4 = INPUT[4]; MOVSEL_5 = INPUT[5]; MOVSEL_6 = INPUT[6]; MOVSEL_7 = INPUT[7];
  //   MOVSEL_8 = INPUT[8]
endmodule

module BOARD_MEM_1 (
  input  RESET,
  input  EN,
  input  CLK,
  input  [8:0] INP,
  output [8:0] STATE
);

  wire [8:0] or_1_out;

  assign or_1_out = INP | STATE;  // OR_Gate or_1, 9 bits wide
  D_Flip_Flop d_ff_1 (.clk(CLK), .D(or_1_out[0]), .Q(STATE[0]), .en(EN), .reset(RESET));  // open: Qn, preset
  D_Flip_Flop d_ff_2 (.clk(CLK), .D(or_1_out[3]), .Q(STATE[3]), .en(EN), .reset(RESET));  // open: Qn, preset
  D_Flip_Flop d_ff_3 (.clk(CLK), .D(or_1_out[6]), .Q(STATE[6]), .en(EN), .reset(RESET));  // open: Qn, preset
  D_Flip_Flop d_ff_4 (.clk(CLK), .D(or_1_out[1]), .Q(STATE[1]), .en(EN), .reset(RESET));  // open: Qn, preset
  D_Flip_Flop d_ff_5 (.clk(CLK), .D(or_1_out[4]), .Q(STATE[4]), .en(EN), .reset(RESET));  // open: Qn, preset
  D_Flip_Flop d_ff_6 (.clk(CLK), .D(or_1_out[7]), .Q(STATE[7]), .en(EN), .reset(RESET));  // open: Qn, preset
  D_Flip_Flop d_ff_7 (.clk(CLK), .D(or_1_out[2]), .Q(STATE[2]), .en(EN), .reset(RESET));  // open: Qn, preset
  D_Flip_Flop d_ff_8 (.clk(CLK), .D(or_1_out[5]), .Q(STATE[5]), .en(EN), .reset(RESET));  // open: Qn, preset
  D_Flip_Flop d_ff_9 (.clk(CLK), .D(or_1_out[8]), .Q(STATE[8]), .en(EN), .reset(RESET));  // open: Qn, preset
endmodule

module COL_DET (
  input  [8:0] STATE,
  input  [8:0] MOV,
  output OK
);

  wire nand_1_out, nand_2_out, nand_3_out, nand_4_out, nand_5_out, nand_6_out, nand_7_out, nand_8_out,
       nand_9_out;

  nand nand_1 (nand_1_out, STATE[0], MOV[0]);
  nand nand_2 (nand_2_out, STATE[3], MOV[3]);
  nand nand_3 (nand_3_out, STATE[6], MOV[6]);
  nand nand_4 (nand_4_out, STATE[1], MOV[1]);
  nand nand_5 (nand_5_out, STATE[4], MOV[4]);
  nand nand_6 (nand_6_out, STATE[7], MOV[7]);
  nand nand_7 (nand_7_out, STATE[2], MOV[2]);
  nand nand_8 (nand_8_out, STATE[5], MOV[5]);
  nand nand_9 (nand_9_out, STATE[8], MOV[8]);
  and and_1 (OK, nand_1_out, nand_4_out, nand_7_out, nand_2_out, nand_5_out, nand_8_out, nand_3_out, nand_6_out, nand_9_out);
endmodule

module P_MOV_OK (
  input  [8:0] B1_state,
  input  [8:0] B2_state,
  input  [8:0] pmov,
  output Player_Move_OK
);

  wire and_1_out, col_det_1_ok, col_det_2_ok, p_selection_ok_1_ok;

  COL_DET col_det_1 (.STATE(B1_state), .MOV(pmov), .OK(col_det_1_ok));
  COL_DET col_det_2 (.STATE(B2_state), .MOV(pmov), .OK(col_det_2_ok));
  P_SELECTION_OK p_selection_ok_1 (.INP(pmov), .OK(p_selection_ok_1_ok));
  and and_1 (and_1_out, col_det_1_ok, col_det_2_ok);
  and and_2 (Player_Move_OK, and_1_out, p_selection_ok_1_ok);

  // Notes on the sheet:
  //   HAS MOV SELECTED
  //   IS LEGAL
endmodule

module P2_SWITCH (
  input  [8:0] PLR_MOV,
  input  [8:0] CPU_MOV,
  input  doAI,
  output [8:0] OUT
);

  Multiplexer #(.width(9), .enable("false")) multiplexer_1 (.in0(PLR_MOV), .in1(CPU_MOV), .out(OUT), .sel(doAI));
endmodule

module WIN_DTCT (
  input  [8:0] STATE,
  output WIN
);

  wire nand_1_out, nand_2_out, nand_3_out, nand_4_out, nand_5_out, nand_6_out, nand_7_out, nand_8_out;

  nand nand_1 (nand_1_out, STATE[1], STATE[0], STATE[2]);
  nand nand_2 (nand_2_out, STATE[0], STATE[3], STATE[6]);
  nand nand_3 (nand_3_out, STATE[0], STATE[4], STATE[8]);
  nand nand_4 (nand_4_out, STATE[3], STATE[4], STATE[5]);
  nand nand_5 (nand_5_out, STATE[1], STATE[4], STATE[7]);
  nand nand_6 (nand_6_out, STATE[2], STATE[4], STATE[6]);
  nand nand_7 (nand_7_out, STATE[6], STATE[7], STATE[8]);
  nand nand_8 (nand_8_out, STATE[2], STATE[5], STATE[8]);
  nand nand_9 (WIN, nand_1_out, nand_4_out, nand_7_out, nand_2_out, nand_5_out, nand_8_out, nand_3_out, nand_6_out);

  // Other names for the same wires on the sheet: B0 = STATE[0]; B1 = STATE[1]; B2 = STATE[2]; B3 = STATE[3];
  //   B4 = STATE[4]; B5 = STATE[5]; B6 = STATE[6]; B7 = STATE[7]; B8 = STATE[8]
endmodule

module END_DTCT (
  input  [8:0] P1,
  input  [8:0] P2,
  output P1_WIN,
  output P2_WIN,
  output DRAW,
  output GAME_OVER
);

  WIN_DTCT win_dtct_1 (.STATE(P1), .WIN(P1_WIN));
  WIN_DTCT win_dtct_2 (.STATE(P2), .WIN(P2_WIN));
  DRAW_DTCT draw_dtct_1 (.P1(P1), .P2(P2), .DRAW(DRAW));
  or or_1 (GAME_OVER, P1_WIN, P2_WIN, DRAW);
endmodule

module DRAW_DTCT (
  input  [8:0] P1,
  input  [8:0] P2,
  output DRAW
);

  wire [8:0] nor_1_out;

  assign nor_1_out = ~(P1 | P2);  // NOR_Gate nor_1, 9 bits wide
  nor nor_2 (DRAW, nor_1_out[0], nor_1_out[1], nor_1_out[2], nor_1_out[3], nor_1_out[4], nor_1_out[5], nor_1_out[6], nor_1_out[7], nor_1_out[8]);
endmodule

module STATE_MACHINE (
  input  CLK,
  input  Player_Move_OK,
  input  P2_is_CPU,
  input  P2_Starts,
  input  GameOver,
  input  RESET,
  output P1_Turn,
  output P2_Turn,
  output P1_Write_Enable,
  output P2_Write_Enable
);

  wire and_1_out, and_2_out, and_3_out, d_ff_1_qn, not_1_out, not_2_out, not_3_out, or_1_out, xor_1_out;

  and and_1 (and_1_out, P2_Turn, P2_is_CPU);
  or or_1 (or_1_out, Player_Move_OK, and_1_out);
  xor xor_1 (xor_1_out, or_1_out, d_ff_1_qn);
  D_Flip_Flop d_ff_1 (
    .clk(CLK), .D(xor_1_out), .Q(P2_Turn), .Qn(d_ff_1_qn), .preset(and_3_out), .reset(and_2_out));  // open: en
  and and_2 (and_2_out, not_1_out, RESET);
  and and_3 (and_3_out, P2_Starts, RESET);
  not not_1 (not_1_out, P2_Starts);
  not not_2 (not_2_out, P2_Turn);
  not not_3 (not_3_out, GameOver);
  and and_4 (P1_Write_Enable, not_2_out, not_3_out, or_1_out);
  and and_5 (P2_Write_Enable, P2_Turn, not_3_out, or_1_out);
  not not_4 (P1_Turn, P2_Turn);
endmodule

module CPU (
  input  [8:0] P1,
  input  [8:0] P2,
  output [8:0] CPU
);

  // Probe on {1'b0, P2, P1}
  ROM #(.addrWidth(19)) rom_1 (.addr({1'b0, P2, P1}), .data(CPU[7:0]));  // open: sel
  nor nor_1 (CPU[8], CPU[0], CPU[1], CPU[2], CPU[3], CPU[4], CPU[5], CPU[6], CPU[7]);
  LED led_1 (.in(CPU[0]));
  LED led_2 (.in(CPU[3]));
  LED led_3 (.in(CPU[6]));
  LED led_4 (.in(CPU[1]));
  LED led_5 (.in(CPU[4]));
  LED led_6 (.in(CPU[7]));
  LED led_7 (.in(CPU[2]));
  LED led_8 (.in(CPU[5]));
  LED led_9 (.in(CPU[8]));

  // Notes on the sheet:
  //   contents of rom_1 (hex, n*v repeats v):
  //   10 10 10 4 10 2 1 ff 10 40 10 4 10 2 1 ff 40 0 80 4 40 2 1 ff 20 20 20 4 20 2 1 ff 10 10 10 4 0 2 1
  //   ff 10 10 10 4 10 2 1 ff 8 8 8 4 8 2 1 9*ff 10 8 10 4 10 2 1 ff 1 ff 1 ff 1 ff 1 ff 4 8 80 4 4*ff 20
  //   ff 20 5*ff 10 8 10 4 0 2 1 ff 10 ff 10 ff 10 ff 1 ff 8 8 8 4 12*ff 10 10 10 4 10 2 1 ff 10 40 10 4
  //   10 2 1 ff 2 2 ff ff 2 2 ff ff 20 20 ff ff 20 2 ff ff 10 10 10 4 0 2 1 ff 10 10 10 4 10 2 1 ff 8 8 ff
  //   ff 8 2 10*ff 0 0 0 4 0 2 1 ff 0 ff 0 ff 0 ff 1 ff 0 0 6*ff 20 7*ff 0 0 0 4 0 2 1 ff 10 ff 10 ff 10
  //   ff ff ff 8 8 14*ff 10 10 10 4 20 2 1 ff 10 40 10 4 20 2 1 ff 1 ff 80 ff 20 ff 1 ff 20 ff 20 ff 20 ff
  //   1 ff 4*4 4*ff 10 10 10 4 4*ff 8 ff 8 13*ff 80 80 80 4 80 2 1 ff 80 ff 80 ff 80 ff 1 ff 80 ff 80 5*ff
  //   20 ff 20 5*ff 80 80 80 4 4*ff 10 ff 10 5*ff 8 ff 8 13*ff 40 40 40 4 40 2 1 ff 40 40 40 4 40 2 1 ff
  //   40 ff ff ff 40 ff ff ff 20 ff ff ff 20 ff ff ff 40 40 40 4 4*ff 10 10 10 5*ff 8 79*ff 10 ff 10 ff 10
  //   ff 10 ff 10 ff 10 ff 10 ff 10 ff 4 ff 80 ff 40 ff 80 ff 20 ff 20 ff 20 ff 20 ff 10 ff 10 ff 0 ff 0
  //   ff 10 ff 10 ff 10 ff 10 ff 8 ff 8 ff 8 ff 8 9*ff 10 ff 10 ff 10 ff 10 ff 10 ff 10 ff 10 ff 10 ff 4
  //   ff 80 5*ff 20 ff 20 5*ff 10 ff 10 ff 0 ff 0 ff 10 ff 10 ff 10 ff 10 ff 8 ff 8 13*ff 10 ff 10 ff 10
  //   ff 10 ff 10 ff 10 ff 10 ff 10 ff 2 ff ff ff 2 ff ff ff 20 ff ff ff 20 ff ff ff 10 ff 10 ff 0 ff 10
  //   ff 10 ff 10 ff 10 ff 10 ff 8 ff ff ff 8 11*ff 0 ff 0 ff 0 ff 0 ff 0 ff 0 ff 0 ff 0 ff 0 7*ff 20 7*ff
  //   0 ff 0 ff 0 ff 0 ff 10 ff 10 ff 10 ff 10 ff 8 15*ff 10 ff 10 ff 20 ff 20 ff 10 ff 10 ff 20 ff 20 ff
  //   40 ff 80 ff 20 ff 80 ff 20 ff 20 ff 20 ff 20 ff 4 ff 4 5*ff 10 ff 10 5*ff 8 ff 8 13*ff 80 ff 80 ff
  //   80 ff 80 ff 80 ff 80 ff 80 ff 80 ff 80 ff 80 5*ff 20 ff 20 5*ff 80 ff 80 5*ff 10 ff 10 5*ff 8 ff 8
  //   13*ff 40 ff 40 ff 40 ff 40 ff 40 ff 40 ff 40 ff 40 ff 40 ff ff ff 40 ff ff ff 20 ff ff ff 20 ff ff
  //   ff 40 ff 40 5*ff 10 ff 10 5*ff 8 79*ff 10 10 ff ff 10 10 ff ff 10 40 ff ff 10 40 ff ff 0 0 ff ff 40
  //   0 ff ff 20 20 ff ff 20 20 ff ff 10 10 ff ff 0 0 ff ff 10 10 ff ff 10 10 ff ff 8 8 ff ff 8 8 10*ff 10
  //   8 ff ff 10 8 ff ff 1 ff ff ff 1 ff ff ff 4 8 6*ff 20 7*ff 10 8 ff ff 0 8 ff ff 10 ff ff ff 10 ff ff
  //   ff 8 8 14*ff 10 10 ff ff 10 10 ff ff 10 40 ff ff 10 40 ff ff 1 0 ff ff 40 0 ff ff 20 20 ff ff 20 20
  //   ff ff 10 10 ff ff 0 0 ff ff 10 10 ff ff 10 10 ff ff 8 8 ff ff 8 8 10*ff 0 0 ff ff 0 0 ff ff 0 ff ff
  //   ff 0 ff ff ff 0 0 6*ff 20 7*ff 0 0 ff ff 0 0 ff ff 10 ff ff ff 10 ff ff ff 8 8 14*ff 10 10 ff ff 20
  //   20 ff ff 10 40 ff ff 20 40 ff ff 1 ff ff ff 20 ff ff ff 20 ff ff ff 20 ff ff ff 4 4 6*ff 10 10 6*ff
  //   8 15*ff 80 80 ff ff 80 80 ff ff 80 ff ff ff 80 ff ff ff 80 7*ff 20 7*ff 80 80 6*ff 10 7*ff 8 15*ff
  //   40 40 ff ff 40 40 ff ff 40 40 ff ff 40 40 ff ff 40 ff ff ff 40 ff ff ff 20 ff ff ff 20 ff ff ff 40
  //   40 6*ff 10 10 6*ff 8 79*ff 4 ff ff ff 10 ff ff ff 4 ff ff ff 10 ff ff ff 4 ff ff ff 40 ff ff ff 4 ff
  //   ff ff 20 ff ff ff 4 ff ff ff 0 ff ff ff 4 ff ff ff 10 ff ff ff 4 ff ff ff 8 11*ff 4 ff ff ff 10 ff
  //   ff ff 4 ff ff ff 10 ff ff ff 4 7*ff 4 7*ff 4 ff ff ff 0 ff ff ff 4 ff ff ff 10 ff ff ff 4 15*ff 4 ff
  //   ff ff 10 ff ff ff 4 ff ff ff 10 ff ff ff 4 ff ff ff 40 ff ff ff 4 ff ff ff 20 ff ff ff 4 ff ff ff 0
  //   ff ff ff 4 ff ff ff 10 ff ff ff 4 ff ff ff 8 11*ff 4 ff ff ff 0 ff ff ff 4 ff ff ff 0 ff ff ff 4
  //   7*ff 4 7*ff 4 ff ff ff 0 ff ff ff 4 ff ff ff 10 ff ff ff 4 15*ff 4 ff ff ff 20 ff ff ff 4 ff ff ff
  //   20 ff ff ff 4 ff ff ff 20 ff ff ff 4 ff ff ff 20 ff ff ff 4 7*ff 4 7*ff 4 15*ff 4 ff ff ff 80 ff ff
  //   ff 4 ff ff ff 80 ff ff ff 4 7*ff 4 7*ff 4 7*ff 4 7*ff 4 15*ff 4 ff ff ff 40 ff ff ff 4 ff ff ff 40
  //   ff ff ff 4 ff ff ff 40 ff ff ff 4 ff ff ff 20 ff ff ff 4 7*ff 4 7*ff 4 79*ff 4*10 4*ff 10 40 10 40
  //   4*ff 1 0 80 80 4*ff 4*20 4*ff 4*10 4*ff 4*10 4*ff 4*8 12*ff 10 8 10 8 4*ff 1 ff 1 5*ff 0 8 80 8 4*ff
  //   20 ff 20 5*ff 10 8 10 8 4*ff 10 ff 10 5*ff 4*8 12*ff 4*10 4*ff 10 40 10 40 4*ff 2 2 6*ff 20 20 6*ff
  //   4*10 4*ff 4*10 4*ff 8 8 14*ff 4*0 4*ff 0 ff 0 5*ff 0 0 6*ff 20 7*ff 4*0 4*ff 10 ff 10 5*ff 8 8 14*ff
  //   4*10 4*ff 10 40 10 40 4*ff 1 ff 80 5*ff 20 ff 20 5*ff 4*10 4*ff 4*10 4*ff 8 ff 8 13*ff 4*80 4*ff 80
  //   ff 80 5*f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
endmodule

module SM_INPUT_DECODE (
  input  P1,
  input  P2,
  input  MOV_OK,
  input  IsAi,
  output [1:0] INPUT_CODE
);

  wire and_2_out, and_3_out;

  and and_1 (INPUT_CODE[0], P1, MOV_OK);
  and and_2 (and_2_out, P2, MOV_OK);
  and and_3 (and_3_out, P2, IsAi);
  or or_1 (INPUT_CODE[1], and_2_out, and_3_out);
endmodule

module SM_OUTPUT_DECODE (
  input  [1:0] StateCode,
  output START_TURN,
  output P1_TURN,
  output P2_TURN,
  output P1_WRT,
  output P2_WRT
);

  wire not_1_out, not_2_out;

  not not_1 (not_1_out, StateCode[0]);
  not not_2 (not_2_out, StateCode[1]);
  nor nor_1 (START_TURN, StateCode[1], StateCode[0]);
  nor nor_2 (P1_TURN, not_1_out, StateCode[1]);
  nor nor_3 (P1_WRT, StateCode[0], not_2_out);

  assign P2_TURN = P1_WRT;
  assign P2_WRT = P1_TURN;
endmodule

module SM_TRANSITION (
  input  [1:0] INPUT,
  input  [1:0] STATE,
  output [1:0] NEW_STATE
);

  wire and_1_out, and_2_out, not_1_out, not_2_out;

  not not_1 (not_1_out, INPUT[0]);
  not not_2 (not_2_out, INPUT[1]);
  and and_1 (and_1_out, STATE[0], not_1_out);
  and and_2 (and_2_out, STATE[1], not_2_out);
  or or_1 (NEW_STATE[0], INPUT[1], and_1_out);
  or or_2 (NEW_STATE[1], INPUT[0], and_2_out);

  // Other names for the same wires on the sheet: B = INPUT[0]; A = INPUT[1]; D = STATE[0]; C = STATE[1]
endmodule

module P_SELECTION_OK (
  input  [8:0] INP,
  output OK
);

  wire and_1_out, nand_1_out, nand_2_out, nand_3_out, nand_4_out, nand_5_out, nand_6_out, nand_7_out,
       nand_8_out, or_1_out, or_2_out, or_3_out, or_4_out, or_5_out, or_6_out, or_7_out, or_8_out;

  or or_1 (or_1_out, INP[1], INP[0]);
  or or_2 (or_2_out, INP[2], or_1_out);
  or or_3 (or_3_out, INP[3], or_2_out);
  or or_4 (or_4_out, INP[4], or_3_out);
  or or_5 (or_5_out, INP[5], or_4_out);
  or or_6 (or_6_out, INP[6], or_5_out);
  or or_7 (or_7_out, INP[7], or_6_out);
  or or_8 (or_8_out, INP[8], or_7_out);
  nand nand_1 (nand_1_out, INP[0], INP[1]);
  nand nand_2 (nand_2_out, or_1_out, INP[2]);
  nand nand_3 (nand_3_out, or_2_out, INP[3]);
  nand nand_4 (nand_4_out, or_3_out, INP[4]);
  nand nand_5 (nand_5_out, or_4_out, INP[5]);
  nand nand_6 (nand_6_out, or_5_out, INP[6]);
  nand nand_7 (nand_7_out, or_6_out, INP[7]);
  nand nand_8 (nand_8_out, or_7_out, INP[8]);
  and and_1 (and_1_out, nand_1_out, nand_2_out, nand_3_out, nand_4_out, nand_5_out, nand_6_out, nand_7_out, nand_8_out);
  and and_2 (OK, and_1_out, or_8_out);
endmodule
